# Fritzing sketch sensing-node (saved by Fritzing 0.9.3b)
breadboards: 1

parts:
  U1 = atmega328 [package=dip]
  XTAL1 = CRYSTAL - kHz [frequency="16 MHz"]
  S1 = SWITCH-MOMENTARY-2 [package=tactile_switch_smd]
  C1 = Capacitor [package=cap-pth-small2]
  C2 = Capacitor [package=cap-pth-small2]
  R1 = Resistor [tolerance=±5% resistance=10k package="0805 [SMD]"]
  Part1 = NRF24L01+ Breakout Board
  LED1 = LED - 3mm [color="Red (633nm)" package="3 mm [THT]"]
  LED2 = LED - 3mm [color="Green (560nm)" package="3 mm [THT]"]
  R2 = Resistor [tolerance=±5% resistance=220 package="0805 [SMD]"]
  DHT1 = DHT11 Humitidy and Temperature Sensor
  R3 = Resistor [tolerance=±5% resistance=220 package=THT]

nets (from the schematic view):
  N1: U1.RESET, S1.2, R1.Pin_0
  N2: U1.D2, R2.Pin_1
  N3: U1.D4, DHT1.DATA
  5V: U1.VCC, R1.Pin_1, DHT1.VDD, R3.Pin_1
  GND: U1.GND#7, S1.1, C1.2, C2.2, Part1.GND, LED1.cathode, LED2.cathode, DHT1.GND
  N4: U1.XLAT1, XTAL1.pin_1, C1.1
  N5: U1.XLAT2, XTAL1.pin_0, C2.1
  N6: U1.D7, Part1.CE
  N7: U1.D8, Part1.CS
  N8: U1.D11_(PWM), Part1.MOSI
  N9: U1.D12, Part1.MISO
  N10: U1.D13, Part1.SCK
  3.3V: Part1.VCC
  N11: LED1.anode, R3.Pin_0
  N12: LED2.anode, R2.Pin_0

custom parts:
  DHT11 Humitidy and Temperature Sensor: DHT11 Humidity and Temperature Sensor
